# Fritzing sketch HandRemote-WiringDiagram (saved by Fritzing 0.9.3b)

parts:
  Part1 = Arduino Uno (Rev3)
  Part3 = Arduino Xbee Libellium Shield
  DFRobot_LCD_keypad_shield1 = LCD keypad Shield
  BuzzerDFR1 = BuzzerDFR0032
  R1 = Resistor [tolerance=±5% resistance=220k package=THT]
  R2 = Resistor [tolerance=±5% resistance=220 package=THT]

nets:
  N1: Part1.D8, DFRobot_LCD_keypad_shield1.D13
  N2: Part1.D4, DFRobot_LCD_keypad_shield1.D2
  N3: Part1.D5_PWM, DFRobot_LCD_keypad_shield1.D3
  N4: Part1.D6_PWM, DFRobot_LCD_keypad_shield1.D11
  N5: Part1.D7, DFRobot_LCD_keypad_shield1.D12
  N6: Part3.M8RXD, DFRobot_LCD_keypad_shield1.VCC
  N7: Part3.M8TXD, DFRobot_LCD_keypad_shield1.GND#19
  N8: DFRobot_LCD_keypad_shield1.GND#4, R2.Pin_0
  N9: DFRobot_LCD_keypad_shield1.Vin, R1.Pin_0
  N10: DFRobot_LCD_keypad_shield1.A1, R1.Pin_1, R2.Pin_1
  N11: DFRobot_LCD_keypad_shield1.D0, BuzzerDFR1.Signal

notes:
  Active Buzzer
  D2 = Signal
  Voltage Divider for Battery Meter
  D0 - RX for XBee
  D1 - TX for XBee
  Used Pins **
  D10 - LCD Backlight
  D9 - LCD Enable
  D8 - LCD RS
  D7 to D4 - LCD DB(0::4)
  Used Pin
  A0 - Keypad Buttons

custom parts:
  LCD keypad Shield: A 2 row LCD shield with buttons, and contrast regulator.
